// Logisim project Pipelined_CPU.circ as structural Verilog: 9 circuits, main circuit Copy_reference
module main (
  input  [15:0] Input
);

  Register PC ();  // open: D, en, Q, clk, clr
  _16_bit_register_file Register_File ();  // open: Reset, Read_Reg_1, Read_Reg_2, Write, Write_Reg_Destination, Write_Data, Read_Reg_1_Output, Read_Reg_2_Output
  Hex_Digit_Display hex_digit_display_1 (.value(Input[15:12]));  // open: dp
  Hex_Digit_Display hex_digit_display_2 (.value(Input[7:4]));  // open: dp
  Hex_Digit_Display hex_digit_display_3 (.value(Input[11:8]));  // open: dp
  Hex_Digit_Display hex_digit_display_4 (.value(Input[3:0]));  // open: dp
endmodule

module _16_bit_register_file (
  input  Reset,
  input  [2:0] Read_Reg_1,
  input  [2:0] Read_Reg_2,
  input  Write,
  input  [2:0] Write_Reg_Destination,
  input  [15:0] Write_Data,
  output [15:0] Read_Reg_1_Output,
  output [15:0] Read_Reg_2_Output
);

  wire demultiplexer_1_out0, demultiplexer_1_out1, demultiplexer_1_out2, demultiplexer_1_out3,
       demultiplexer_1_out4, demultiplexer_1_out5, demultiplexer_1_out6, demultiplexer_1_out7;
  wire [15:0] r0_q, r1_q, r2_q, r3_q, r4_q, r5_q, r6_q;

  Demultiplexer #(.select(3)) demultiplexer_1 (
    .out0(demultiplexer_1_out0), .out1(demultiplexer_1_out1), .out2(demultiplexer_1_out2),
    .out3(demultiplexer_1_out3), .out4(demultiplexer_1_out4), .out5(demultiplexer_1_out5),
    .out6(demultiplexer_1_out6), .out7(demultiplexer_1_out7), .in(Write), .sel(Write_Reg_Destination));  // open: en
  Register #(.width(16)) r0 (.D(Write_Data), .Q(r0_q), .clk(demultiplexer_1_out0), .clr(Reset));  // open: en
  Register #(.width(16)) r1 (.D(Write_Data), .Q(r1_q), .clk(demultiplexer_1_out1), .clr(Reset));  // open: en
  Register #(.width(16)) r2 (.D(Write_Data), .Q(r2_q), .clk(demultiplexer_1_out2), .clr(Reset));  // open: en
  Register #(.width(16)) r3 (.D(Write_Data), .Q(r3_q), .clk(demultiplexer_1_out3), .clr(Reset));  // open: en
  Register #(.width(16)) r4 (.D(Write_Data), .Q(r4_q), .clk(demultiplexer_1_out4), .clr(Reset));  // open: en
  Register #(.width(16)) r5 (.D(Write_Data), .Q(r5_q), .clk(demultiplexer_1_out5), .clr(Reset));  // open: en
  Register #(.width(16)) r6 (.D(Write_Data), .Q(r6_q), .clk(demultiplexer_1_out6), .clr(Reset));  // open: en
  Register #(.width(16)) r7 (.D(Write_Data), .Q(r3_q), .clk(demultiplexer_1_out7), .clr(Reset));  // open: en
  Multiplexer #(.select(3), .width(16), .enable("false")) multiplexer_1 (
    .in0(r0_q), .in1(r1_q), .in2(r2_q), .in3(r3_q), .in4(r4_q), .in5(r5_q), .in6(r6_q), .in7(r3_q),
    .out(Read_Reg_1_Output), .sel(Read_Reg_1));
  Multiplexer #(.select(3), .width(16), .enable("false")) multiplexer_2 (
    .in0(r0_q), .in1(r1_q), .in2(r2_q), .in3(r3_q), .in4(r4_q), .in5(r5_q), .in6(r6_q), .in7(r3_q),
    .out(Read_Reg_2_Output), .sel(Read_Reg_2));
endmodule

module Instruction_Memory (
  input  [7:0] Address,
  output [15:0] Output
);

  ROM #(.dataWidth(16)) rom_1 (.addr(Address), .data(Output), .sel(1'b1));
endmodule

module Data_Memory (
  input  [7:0] Address,
  input  [15:0] Data_In,
  output [15:0] Data_Out
);

  RAM #(.dataWidth(16), .bus("separate")) ram_1 (
    .addr(Address), .din(Data_In), .data(Data_Out), .sel(1'b1));  // open: str, clk, ld, clr
endmodule

module ALU (
  input  [15:0] Input_A,
  input  [15:0] Input_B,
  output [15:0] ALU_Output
);

  wire [15:0] adder_1_out, comparator_1_eq, comparator_1_gt, comparator_1_lt;

  Adder #(.width(16)) adder_1 (.a(Input_A), .b(Input_B), .out(adder_1_out));  // open: cin, cout
  Subtractor #(.width(16)) subtractor_1 (.a(Input_A), .b(Input_B), .out(adder_1_out));  // open: bin, bout
  Comparator #(.width(16)) comparator_1 (
    .a(Input_A), .b(Input_B), .gt(comparator_1_gt[0]), .eq(comparator_1_eq[0]), .lt(comparator_1_lt[0]));
  Multiplexer #(.select(3), .width(16)) multiplexer_1 (
    .in0(adder_1_out), .in1(adder_1_out), .in2(comparator_1_gt), .in3(comparator_1_eq),
    .in4(comparator_1_lt), .out(ALU_Output));  // open: in5, in6, in7, sel, en
  // Pins of 1 and 16 bits meet at comparator_1_gt
  // Pins of 1 and 16 bits meet at comparator_1_eq
  // Pins of 1 and 16 bits meet at comparator_1_lt
endmodule

module Sign_Extender (
  input  Unsigned,
  input  [7:0] Immediate,
  output [15:0] SignExtendedImm
);

  wire [15:0] bit_extender_1_out, bit_extender_2_out;

  assign bit_extender_1_out = {{8{Immediate[7]}}, Immediate};  // Bit_Extender bit_extender_1
  assign bit_extender_2_out = {{8{1'b0}}, Immediate};  // Bit_Extender bit_extender_2
  Multiplexer #(.width(16), .disabled(0), .enable("false")) multiplexer_1 (
    .in0(bit_extender_1_out), .in1(bit_extender_2_out), .out(SignExtendedImm), .sel(Unsigned));
endmodule

module Copy_reference (
);

  wire button_1_out, clock_1_out, Decoder_p1, Decoder_p2, Decoder_p4, Decoder_p5, Decoder_p6, Decoder_p7,
       Decoder_p8, Instruction_Splitter_p2, Instruction_Splitter_p3, Instruction_Splitter_p4,
       Instruction_Splitter_p5, Instruction_Splitter_p6, Instruction_Splitter_p7, Instruction_Splitter_p8,
       not_1_out, Registers_p5, ResultToLess_p2, ResultToLess_p5, ResultToLess_p7, ResultToLess_p8,
       ResultToLess_p9, ResultToLess_p10, ResultToLess_p11, ResultToLess_p12, ResultToLess_p13;
  wire [7:0] adder_1_out, Instruction_Splitter_p9, multiplexer_2_out, multiplexer_4_out, PC_q,
       RegistertoAddress_2_p2, RegistertoAddress_p2;
  wire [15:0] ALU_p3, bit_extender_1_out, IF_ID_Label_out_3, multiplexer_1_out, multiplexer_5_out,
       multiplexer_7_out, ram_1_data, register_1_q, Registers_p4, Registers_p7, Registers_p8,
       ResultToLess_p1, rom_1_data, Shifter_p6, Sign_Extend_p3;

  Clock clock_1 (.out(clock_1_out));
  Register PC (.D(multiplexer_4_out), .en(not_1_out), .Q(PC_q), .clk(clock_1_out), .clr(button_1_out));
  not not_1 (not_1_out, ResultToLess_p9);
  Button button_1 (.out(button_1_out));
  Adder adder_1 (.a(PC_q), .b(8'h1), .out(adder_1_out));  // open: cin, cout
  ROM #(.dataWidth(16)) rom_1 (.addr(PC_q), .data(rom_1_data), .sel(1'b1));
  IF_ID_Buffer IF_ID_Label (.in_1(rom_1_data), .ClockIn(clock_1_out), .out_3(IF_ID_Label_out_3));
  // InstructionSplitter Instruction_Splitter: pin names not known; wires that end beside it: IF_ID_Label_out_3, Instruction_Splitter_p2, Instruction_Splitter_p3, Instruction_Splitter_p4, Instruction_Splitter_p5, Instruction_Splitter_p6, Instruction_Splitter_p7, Instruction_Splitter_p8, Instruction_Splitter_p9
  // SignExtend Sign_Extend: pin names not known; wires that end beside it: Instruction_Splitter_p8, Instruction_Splitter_p9, Sign_Extend_p3
  // ResultToLess ResultToLess: pin names not known; wires that end beside it: ResultToLess_p1, ResultToLess_p2, Instruction_Splitter_p2, Instruction_Splitter_p7, ResultToLess_p5, ResultToLess_p2, ResultToLess_p7, ResultToLess_p8, ResultToLess_p9, ResultToLess_p10, ResultToLess_p11, ResultToLess_p12, ResultToLess_p13
  // RegisterFile Registers: pin names not known; wires that end beside it: Instruction_Splitter_p3, Instruction_Splitter_p4, Instruction_Splitter_p5, Registers_p4, Registers_p5, clock_1_out, Registers_p7, Registers_p8
  // Decoder Decoder: pin names not known; wires that end beside it: Decoder_p1, Decoder_p2, Registers_p5, Decoder_p4, Decoder_p5, Decoder_p6, Decoder_p7, Decoder_p8
  // ALUtoPC RegistertoAddress: pin names not known; wires that end beside it: Registers_p7, RegistertoAddress_p2
  Multiplexer #(.width(16), .disabled(0), .enable("false")) multiplexer_1 (
    .in0(Registers_p8), .in1(Sign_Extend_p3), .out(multiplexer_1_out), .sel(Decoder_p5));
  Multiplexer #(.width(8), .disabled(0), .enable("false")) multiplexer_2 (
    .in0(adder_1_out), .in1(Instruction_Splitter_p9), .out(multiplexer_2_out), .sel(Decoder_p7));
  // sixteen_bit_ALU ALU: pin names not known; wires that end beside it: Decoder_p4, Registers_p7, ALU_p3, ResultToLess_p5, ResultToLess_p1
  Multiplexer #(.width(16), .disabled(0), .enable("false")) multiplexer_3 (
    .in0(multiplexer_1_out), .in1({16{1'b0}}), .out(ALU_p3), .sel(Decoder_p8));
  Multiplexer #(.width(8), .disabled(0), .enable("false")) multiplexer_4 (
    .in0(multiplexer_2_out), .in1(RegistertoAddress_p2), .out(multiplexer_4_out), .sel(Decoder_p6));
  // ALUtoPC RegistertoAddress_2: pin names not known; wires that end beside it: Registers_p8, RegistertoAddress_2_p2
  // Shifter Shifter: pin names not known; wires that end beside it: Instruction_Splitter_p7, Registers_p7, Registers_p8, Decoder_p1, Instruction_Splitter_p6, Shifter_p6
  Multiplexer #(.width(16), .disabled(0), .enable("false")) multiplexer_5 (
    .in0(multiplexer_7_out), .in1(Shifter_p6), .out(multiplexer_5_out), .sel(Decoder_p2));
  Multiplexer #(.width(16), .disabled(0), .enable("false")) multiplexer_6 (
    .in0(multiplexer_5_out), .in1(bit_extender_1_out), .out(Registers_p4), .sel(ResultToLess_p13));
  assign bit_extender_1_out = {{8{1'b0}}, adder_1_out};  // Bit_Extender bit_extender_1
  RAM #(.dataWidth(16), .bus("separate")) ram_1 (
    .addr(RegistertoAddress_2_p2), .din(Registers_p7), .data(ram_1_data), .str(ResultToLess_p7), .sel(1'b1),
    .clk(clock_1_out), .ld(ResultToLess_p12));  // open: clr
  Multiplexer #(.width(16), .disabled(0), .enable("false")) multiplexer_7 (
    .in0(ResultToLess_p1), .in1(ram_1_data), .out(multiplexer_7_out), .sel(ResultToLess_p8));
  Hex_Digit_Display hex_digit_display_1 (.value(register_1_q[15:12]));  // open: dp
  Hex_Digit_Display hex_digit_display_2 (.value(register_1_q[11:8]));  // open: dp
  Register #(.width(16)) register_1 (
    .D(Registers_p7), .en(ResultToLess_p11), .Q(register_1_q), .clk(clock_1_out));  // open: clr
  LED Halt (.in(ResultToLess_p10));
  Hex_Digit_Display hex_digit_display_3 (.value(register_1_q[7:4]));  // open: dp
  Hex_Digit_Display hex_digit_display_4 (.value(register_1_q[3:0]));  // open: dp

  // Notes on the sheet:
  //   contents of rom_1 (hex, n*v repeats v):
  //   1 1104 241 1303 40 f000 241 1300 481 1503 281 6c1 1705 2c1 f200 901 1900 18ff f800 b41 1bf0 1b0f
  //   fa00 d81 1d19 fc1 1f20 3dc0 fc00 1 11e0 241 1378 3041 f000 481 150d 6c1 1708 44c0 f400 901 1910 b41
  //   1b04 4941 f800 d81 1d02 5c02 fc00 fc1 1f10 5e03 fe00 1 1140 61c1 63c0 f200 481 15ff 6c1 1701 845b
  //   865b 901 1900 985f b41 1b00 d81 1d00 1ce9 aa63 ac63 fc1 1f00 1 1119 be67 b067 e054 7000 c259 6c1
  //   170a f600 7000 d200 7000 fc1 1f01 fe00 7000 fc1 1f02 fe00 7000 fc1 1f03 fe00 7000 fc1 1f04 fe00 7000
endmodule

module IF_ID_Buffer (
  input  [15:0] in_1,
  input  ClockIn,
  output [15:0] out_3
);

  Register #(.width(16)) Instruction_Memory (.D(in_1), .Q(out_3), .clk(ClockIn));  // open: en, clr
endmodule

module ID_EX_Buffer (
  input  [15:0] Read_Data_1,
  input  [15:0] Read_Data_2,
  input  Clock,
  output [15:0] Read_Data_1_2,
  output [15:0] Read_Data_2_2
);

  Register #(.width(16)) u_Read_Data_1 (.D(Read_Data_1), .Q(Read_Data_1_2), .clk(Clock));  // open: en, clr
  Register #(.width(16)) u_Read_Data_2 (.D(Read_Data_2), .Q(Read_Data_2_2), .clk(Clock));  // open: en, clr
endmodule
